# Fritzing sketch looper (saved by Fritzing 0.9.3b)

parts:
  Composant1 = Arduino Uno (Rev3) - ICSP
  LED2 = smd LED [color="Red (633nm)" package="1206 [SMD]"]
  LED3 = smd LED [color="Green (555nm)" package="1206 [SMD]"]
  LED4 = smd LED [color="Red (633nm)" package="1206 [SMD]"]
  LED5 = smd LED [color="Green (565nm)" package="1206 [SMD]"]
  LED6 = smd LED [color="Green (565nm)" package="1206 [SMD]"]
  LED7 = smd LED [color="Red (633nm)" package="1206 [SMD]"]
  LED8 = smd LED [color="Green (565nm)" package="1206 [SMD]"]
  LED9 = smd LED [color="Red (633nm)" package="1206 [SMD]"]
  R1 = Resistor [tolerance=±5% resistance=1.7k package=THT]
  R2 = Resistor [tolerance=±5% resistance=1.7k package=THT]
  R3 = Resistor [tolerance=±5% resistance=1.7k package=THT]
  R4 = Resistor [tolerance=±5% resistance=1.7k package=THT]
  R5 = Resistor [tolerance=±5% resistance=1.7k package=THT]
  R6 = Resistor [tolerance=±5% resistance=1.7k package=THT]
  R7 = Resistor [tolerance=±5% resistance=1.7k package=THT]
  R8 = Resistor [tolerance=±5% resistance=1.7k package=THT]
  U2 = SWITCH_SPDT [package=kps-1290]
  U3 = SWITCH_SPDT [package=kps-1290]
  U4 = SWITCH_SPDT [package=kps-1290]
  U5 = SWITCH_SPDT [package=kps-1290]

nets:
  N1: Composant1.ICSP_MOSI, Composant1.D11_PWM/MOSI, R7.Pin_0
  N2: Composant1.D8, R5.Pin_0
  N3: Composant1.D9_PWM, R6.Pin_0
  N4: Composant1.D10_PWM/SS, U4.P
  N5: Composant1.D12/MISO, R8.Pin_0
  N6: Composant1.D13/SCK, U5.P
  N7: Composant1.GND, LED2.cathode, LED3.cathode, LED4.cathode, LED5.cathode, LED6.cathode, LED7.cathode, LED8.cathode, LED9.cathode, U5.S
  N8: Composant1.D2, R2.Pin_0
  N9: Composant1.D3_PWM, R1.Pin_0
  N10: Composant1.D4, U2.P
  N11: Composant1.D5_PWM, R3.Pin_0
  N12: Composant1.D6_PWM, R4.Pin_0
  N13: Composant1.D7, U3.P
  N14: LED2.anode, R4.Pin_1
  N15: LED3.anode, R3.Pin_1
  N16: LED4.anode, R1.Pin_1
  N17: LED5.anode, R2.Pin_1
  N18: LED6.anode, R5.Pin_1
  N19: LED7.anode, R6.Pin_1
  N20: LED8.anode, R7.Pin_1
  N21: LED9.anode, R8.Pin_1
